# Fritzing sketch sketch (saved by Fritzing 0.9.3b)
breadboards: 1

parts:
  Adafruit_HUZZAH_ESP8266_Breakout1 = Adafruit HUZZAH ESP8266 Breakout [part_number=2471]
  S1 = Pushbutton [package="[THT]"]
  LED1 = RGB LED (com. cathode, rgb) [package="5 mm [THT]"]
  S2 = Toggle Switch [package=THT]
  U1 = POT [package=pot_mammoth]
  L1 = Solenoid
  Q1 = NPN-Transistor [package="TO92 [THT]"]
  VCC2 = Battery block 9V
  J1 = Piezo Speaker
  R1 = Resistor [tolerance=±5% resistance=1k package=THT]
  R2 = Resistor [tolerance=±5% resistance=220 package=THT]
  R3 = Resistor [tolerance=±5% resistance=220 package=THT]
  R4 = Resistor [tolerance=±5% resistance=560 package=THT]
  VCC3 = 4 x AAA Battery Mount

nets:
  N1: Adafruit_HUZZAH_ESP8266_Breakout1.GND, U1.A, L1.pin1, Q1.E, J1.pin2, R1.Pin_0, R2.Pin_1, R3.Pin_0, VCC3.+
  N2: Adafruit_HUZZAH_ESP8266_Breakout1.VBat, VCC3.-
  N3: Adafruit_HUZZAH_ESP8266_Breakout1.#13, LED1.red_anode
  N4: Adafruit_HUZZAH_ESP8266_Breakout1.#12, LED1.green_anode
  N5: Adafruit_HUZZAH_ESP8266_Breakout1.#14, LED1.blue_anode
  N6: Adafruit_HUZZAH_ESP8266_Breakout1.A, U1.S
  N7: Adafruit_HUZZAH_ESP8266_Breakout1.#5, S2.COM
  N8: Adafruit_HUZZAH_ESP8266_Breakout1.#4, S1.Pin_1, S1.Pin_2, R1.Pin_1
  N9: Adafruit_HUZZAH_ESP8266_Breakout1.3V, S1.Pin_3, S1.Pin_4, R4.Pin_0
  N10: LED1.common_cathode, R2.Pin_0
  N11: S2.L1, Q1.B
  N12: S2.L2, J1.pin1
  N13: U1.E, R3.Pin_1, R4.Pin_1
  N14: L1.pin2, VCC2.+
  N15: Q1.C, VCC2.-
